// Logisim project ALU.circ as structural Verilog: 1 circuit, main circuit main
module main (
  input  [6:0] funct7,
  input  AddOveride,
  input  [2:0] funct3,
  input  [31:0] s1,
  input  [31:0] s2,
  output [31:0] d
);

  wire adder_1_cout, comparator_1_eq, comparator_2_lt, comparator_3_lt, multiplexer_1_out;
  wire [2:0] multiplexer_4_out;
  wire [4:0] bitselector_1_out;
  wire [31:0] adder_1_out, and_1_out, bit_extender_1_out, bit_extender_2_out, multiplexer_2_out,
       multiplexer_3_out, or_1_out, shifter_1_out, shifter_2_out, shifter_3_out, subtractor_1_out, xor_1_out;

  // Probe on bitselector_1_out
  BitSelector #(.group(5), .width(32)) bitselector_1 (.in(s2), .out(bitselector_1_out), .sel(3'b000));
  Comparator #(.width(7)) comparator_1 (.a(funct7), .b(7'b0100000), .eq(comparator_1_eq));  // open: gt, lt
  Comparator #(.mode("unsigned"), .width(32)) comparator_2 (.a(s1), .b(s2), .lt(comparator_2_lt));  // open: gt, eq
  Comparator #(.width(32)) comparator_3 (.a(s1), .b(s2), .lt(comparator_3_lt));  // open: gt, eq
  assign xor_1_out = s1 ^ s2;  // XOR_Gate xor_1, 32 bits wide
  assign and_1_out = s1 & s2;  // AND_Gate and_1, 32 bits wide
  assign or_1_out = s1 | s2;  // OR_Gate or_1, 32 bits wide
  Adder #(.width(32)) adder_1 (.a(s1), .b(s2), .out(adder_1_out), .cout(adder_1_cout));  // open: cin
  Subtractor #(.width(32)) subtractor_1 (.a(s1), .b(s2), .out(subtractor_1_out), .bin(adder_1_cout));  // open: bout
  Shifter #(.width(32)) shifter_1 (.in(s1), .\dist (bitselector_1_out), .out(shifter_1_out));
  Shifter #(.shift("lr"), .width(32)) shifter_2 (.in(s1), .\dist (bitselector_1_out), .out(shifter_2_out));
  Shifter #(.shift("ar"), .width(32)) shifter_3 (.in(s1), .\dist (bitselector_1_out), .out(shifter_3_out));
  Multiplexer #(.enable("false")) multiplexer_1 (
    .in0(comparator_1_eq), .in1(1'b0), .out(multiplexer_1_out), .sel(AddOveride));
  assign bit_extender_1_out = {{31{1'b0}}, comparator_2_lt};  // Bit_Extender bit_extender_1
  assign bit_extender_2_out = {{31{1'b0}}, comparator_3_lt};  // Bit_Extender bit_extender_2
  Multiplexer #(.enable("false"), .width(32)) multiplexer_2 (
    .in0(adder_1_out), .in1(subtractor_1_out), .out(multiplexer_2_out), .sel(multiplexer_1_out));
  Multiplexer #(.enable("false"), .width(32)) multiplexer_3 (
    .in0(shifter_2_out), .in1(shifter_3_out), .out(multiplexer_3_out), .sel(multiplexer_1_out));
  Multiplexer #(.enable("false"), .width(3)) multiplexer_4 (
    .in0(funct3), .in1(3'b000), .out(multiplexer_4_out), .sel(AddOveride));
  Multiplexer #(.enable("false"), .select(3), .width(32)) multiplexer_5 (
    .in0(multiplexer_2_out), .in1(shifter_1_out), .in2(bit_extender_2_out), .in3(bit_extender_1_out),
    .in4(xor_1_out), .in5(multiplexer_3_out), .in6(or_1_out), .in7(and_1_out), .out(d),
    .sel(multiplexer_4_out));
endmodule
