// Logisim project BranchCalc.circ as structural Verilog: 1 circuit, main circuit main
module main (
  input  [2:0] f3,
  input  [31:0] rs1,
  input  [31:0] rs2,
  input  b_type,
  output Take_branch
);

  wire comparator_1_eq, comparator_1_gt, comparator_1_lt, comparator_2_gt, comparator_2_lt,
       multiplexer_1_out, not_1_out;

  not not_1 (not_1_out, comparator_1_eq);
  Comparator #(.width(32)) comparator_1 (
    .a(rs1), .b(rs2), .gt(comparator_1_gt), .eq(comparator_1_eq), .lt(comparator_1_lt));
  Comparator #(.mode("unsigned"), .width(32)) comparator_2 (
    .a(rs1), .b(rs2), .gt(comparator_2_gt), .lt(comparator_2_lt));  // open: eq
  Multiplexer #(.enable("false"), .select(3)) multiplexer_1 (
    .in0(comparator_1_eq), .in1(not_1_out), .in4(comparator_1_lt), .in5(comparator_1_gt),
    .in6(comparator_2_lt), .in7(comparator_2_gt), .out(multiplexer_1_out), .sel(f3));  // open: in2, in3
  Multiplexer #(.enable("false")) multiplexer_2 (.in0(1'b0), .in1(multiplexer_1_out), .out(Take_branch), .sel(b_type));
endmodule
