// Logisim project DataMemory.circ as structural Verilog: 1 circuit, main circuit main
module main (
  input  [31:0] address,
  input  [4:0] byte_writes,
  input  clk,
  input  [31:0] data_in,
  output [31:0] data_out
);

  wire comparator_1_lt;
  wire [7:0] undriven, undriven_2, undriven_3, undriven_4;
  wire [9:0] bitselector_1_out;
  wire [23:0] bitselector_2_out;
  wire [31:0] rom_1_data;

  // Probe on bitselector_1_out
  BitSelector #(.group(10), .width(32)) bitselector_1 (.in(address), .out(bitselector_1_out), .sel(2'b00));
  BitSelector #(.group(24), .width(32)) bitselector_2 (.in(address), .out(bitselector_2_out), .sel(1'b0));
  ROM #(.addrWidth(10), .dataWidth(32)) rom_1 (.addr(bitselector_1_out), .data(rom_1_data));
  // RAM #(.addrWidth(24), .line("quad")) ram_1: pin names not known; wires that end beside it: bitselector_2_out, clk
  Comparator #(.mode("unsigned"), .width(32)) comparator_1 (
    .a(address), .b(32'h4000), .lt(comparator_1_lt));  // open: gt, eq
  Multiplexer #(.enable("false"), .width(32)) multiplexer_1 (
    .in0({undriven_4, undriven_3, undriven_2, undriven}), .in1(rom_1_data), .out(data_out),
    .sel(comparator_1_lt));

  // Notes on the sheet:
  //   contents of rom_1 (hex, n*v repeats v):
  //   ffffffff
endmodule
