// Logisim project InstructionMemory.circ as structural Verilog: 1 circuit, main circuit main
module main (
  input  [31:0] address,
  output [31:0] data_out
);

  wire [9:0] bitselector_1_out;

  BitSelector #(.group(10), .width(32)) bitselector_1 (.in(address), .out(bitselector_1_out), .sel(2'b00));
  ROM #(.addrWidth(10), .dataWidth(32)) rom_1 (.addr(bitselector_1_out), .data(data_out));

  // Notes on the sheet:
  //   contents of rom_1 (hex, n*v repeats v):
  //   100093 1000113 11100193 208233 401102b3 11c333 1163b3 11f433 1094b3 115533 401155b3 20a633 1126b3 93
  //   113 193 213 293 313 393 413 493 513 593 613 693 ff00093 770c113 7716193 f0f213 109293 10d313
  //   4010d393 a413 1ff0a493 93 113 193 213 293 313 393 413 493 fff08093 102223 402103 100423 800183
  //   101623 c01203 404283 405303
endmodule
