// Logisim project InstructionShim.circ as structural Verilog: 13 circuits, main circuit InstructionDecoder
module InstructionDecoder (
  input  [31:0] Instruction,
  output [2:0] \type ,
  output [6:0] opcode,
  output [4:0] rd,
  output [2:0] funct3,
  output [4:0] rs1,
  output [4:0] rs2,
  output [31:0] IImm,
  output [6:0] funct7,
  output [31:0] SImm,
  output [31:0] BImm,
  output [31:0] UImm,
  output [31:0] JImm
);

  IImm iimm_1 (.out_2(IImm), .in_1(Instruction));
  SImm simm_1 (.out_2(SImm), .in_1(Instruction));
  BImm bimm_1 (.out_2(BImm), .in_1(Instruction));
  UImm uimm_1 (.out_2(UImm), .in_1(Instruction));
  JImm jimm_1 (.out_2(JImm), .in_1(Instruction));
  // Probe on \type 
  TypeGetter typegetter_1 (.out_2(\type ), .in_1(Instruction[6:0]));

  assign funct3 = Instruction[14:12];
  assign funct7 = Instruction[31:25];
  assign opcode = Instruction[6:0];
  assign rd = Instruction[11:7];
  assign rs1 = Instruction[19:15];
  assign rs2 = Instruction[24:20];

  // Notes on the sheet:
  //   R=0
  //   I=1
  //   S=2
  //   B=3
  //   U=4
  //   J=5
endmodule

module TypeGetter (
  input  [6:0] in_1,
  output [2:0] out_2
);

  wire isbtype_1_out_2, isitype_1_out_2, isjtype_1_out_2, isrtype_1_out_2, isstype_1_out_2, isutype_1_out_2;

  isRType isrtype_1 (.out_2(isrtype_1_out_2), .in_1(in_1));
  isIType isitype_1 (.out_2(isitype_1_out_2), .in_1(in_1));
  isSType isstype_1 (.out_2(isstype_1_out_2), .in_1(in_1));
  isBType isbtype_1 (.out_2(isbtype_1_out_2), .in_1(in_1));
  isUType isutype_1 (.out_2(isutype_1_out_2), .in_1(in_1));
  isJType isjtype_1 (.out_2(isjtype_1_out_2), .in_1(in_1));
  Priority_Encoder priority_encoder_1 (
    .in0(isrtype_1_out_2), .in1(isitype_1_out_2), .in2(isstype_1_out_2), .in3(isbtype_1_out_2),
    .in4(isutype_1_out_2), .in5(isjtype_1_out_2), .out(out_2));  // open: in6, in7, en_in, gs, en_out
endmodule

module isRType (
  input  [6:0] in_1,
  output out_2
);

  Comparator #(.width(7)) comparator_1 (.a(7'b0110011), .b(in_1), .eq(out_2));  // open: gt, lt
endmodule

module isIType (
  input  [6:0] in_1,
  output out_2
);

  wire comparator_1_eq, comparator_2_eq, comparator_3_eq;

  Comparator #(.width(7)) comparator_1 (.a(7'b0000011), .b(in_1), .eq(comparator_1_eq));  // open: gt, lt
  Comparator #(.width(7)) comparator_2 (.a(7'b0010011), .b(in_1), .eq(comparator_2_eq));  // open: gt, lt
  Comparator #(.width(7)) comparator_3 (.a(7'b1100111), .b(in_1), .eq(comparator_3_eq));  // open: gt, lt
  or or_1 (out_2, comparator_1_eq, comparator_2_eq, comparator_3_eq);
endmodule

module isSType (
  input  [6:0] in_1,
  output out_2
);

  Comparator #(.width(7)) comparator_1 (.a(7'b0100011), .b(in_1), .eq(out_2));  // open: gt, lt
endmodule

module isBType (
  input  [6:0] in_1,
  output out_2
);

  Comparator #(.width(7)) comparator_1 (.a(7'b1100011), .b(in_1), .eq(out_2));  // open: gt, lt
endmodule

module isUType (
  input  [6:0] in_1,
  output out_2
);

  wire comparator_1_eq, comparator_2_eq;

  Comparator #(.width(7)) comparator_1 (.a(7'b0110111), .b(in_1), .eq(comparator_1_eq));  // open: gt, lt
  Comparator #(.width(7)) comparator_2 (.a(7'b0010111), .b(in_1), .eq(comparator_2_eq));  // open: gt, lt
  or or_1 (out_2, comparator_1_eq, comparator_2_eq);
endmodule

module isJType (
  input  [6:0] in_1,
  output out_2
);

  Comparator #(.width(7)) comparator_1 (.a(7'b1101111), .b(in_1), .eq(out_2));  // open: gt, lt
endmodule

module IImm (
  input  [31:0] in_1,
  output [31:0] out_2
);


  assign out_2 = {{21{in_1[31]}}, in_1[30:20]};
endmodule

module SImm (
  input  [31:0] in_1,
  output [31:0] out_2
);


  assign out_2 = {{21{in_1[31]}}, in_1[30:25], in_1[11:7]};
endmodule

module BImm (
  input  [31:0] in_1,
  output [31:0] out_2
);


  assign out_2 = {{20{in_1[31]}}, in_1[7], in_1[30:25], in_1[11:8], 1'b0};
endmodule

module UImm (
  input  [31:0] in_1,
  output [31:0] out_2
);


  assign out_2 = {in_1[31:12], {12{1'b0}}};
endmodule

module JImm (
  input  [31:0] in_1,
  output [31:0] out_2
);


  assign out_2 = {{12{in_1[31]}}, in_1[19:12], in_1[20], in_1[30:21], 1'b0};
endmodule
