// Logisim project LoadSelector.circ as structural Verilog: 1 circuit, main circuit main
module main (
  input  [31:0] in_1,
  input  [2:0] in_2,
  output [31:0] out_3
);

  wire bitselector_5_out, bitselector_6_out;
  wire [7:0] bitselector_1_out, bitselector_3_out;
  wire [15:0] bit_extender_2_out, bitselector_2_out, bitselector_4_out;
  wire [23:0] bit_extender_1_out;

  BitSelector #(.group(8), .width(32)) bitselector_1 (.in(in_1), .out(bitselector_1_out), .sel(2'b00));
  BitSelector #(.group(16), .width(32)) bitselector_2 (.in(in_1), .out(bitselector_2_out), .sel(1'b0));
  BitSelector #(.group(8), .width(32)) bitselector_3 (.in(in_1), .out(bitselector_3_out), .sel(2'b00));
  BitSelector #(.group(16), .width(32)) bitselector_4 (.in(in_1), .out(bitselector_4_out), .sel(1'b0));
  assign bit_extender_1_out = {{23{bitselector_5_out}}, bitselector_5_out};  // Bit_Extender bit_extender_1
  BitSelector bitselector_5 (.in(bitselector_1_out), .out(bitselector_5_out), .sel(3'b111));
  assign bit_extender_2_out = {{15{bitselector_6_out}}, bitselector_6_out};  // Bit_Extender bit_extender_2
  BitSelector #(.width(16)) bitselector_6 (.in(bitselector_2_out), .out(bitselector_6_out), .sel(4'b1111));
  // Probe on {bit_extender_1_out, bitselector_1_out}
  // Probe on {bit_extender_2_out, bitselector_2_out}
  // Probe on in_1
  // Probe on {{24{1'b0}}, bitselector_3_out}
  // Probe on {{16{1'b0}}, bitselector_4_out}
  Multiplexer #(.enable("false"), .select(3), .width(32)) multiplexer_1 (
    .in0({bit_extender_1_out, bitselector_1_out}), .in1({bit_extender_2_out, bitselector_2_out}), .in2(in_1),
    .in4({{24{1'b0}}, bitselector_3_out}), .in5({{16{1'b0}}, bitselector_4_out}), .out(out_3), .sel(in_2));  // open: in3, in6, in7
endmodule
