// Logisim project RV32I.circ as structural Verilog: 1 circuit, main circuit main
module main (
  input  reset
);

  wire ALUToPC, B, bitselector_1_out, clk, fADD, I, J, jalr, loadData, push, R, takeBranch, U, usePC, wRD;
  wire [2:0] f3, \type ;
  wire [4:0] dWrites, instructiondecoder_1_rd, instructiondecoder_1_rs1, instructiondecoder_1_rs2;
  wire [6:0] f7, opcode;
  wire [31:0] adder_1_out, adder_2_out, adder_3_out, B_Imm, I_Imm, J_Imm, main_1_data_out, main_2_rs1,
       main_2_rs2, main_4_d, main_6_data_out, main_7_out_3, multiplexer_1_out, multiplexer_2_out,
       multiplexer_3_out, multiplexer_4_out, multiplexer_5_out, multiplexer_6_out, multiplexer_7_out, PC_q,
       S_Imm, shifter_1_out, shifter_2_out, U_Imm;

  // Probe on multiplexer_1_out
  Multiplexer #(.enable("false"), .width(32)) multiplexer_1 (
    .in0(adder_1_out), .in1(shifter_2_out), .out(multiplexer_1_out), .sel(ALUToPC));
  Register #(.width(32)) PC (.D(multiplexer_1_out), .Q(PC_q), .clk(clk), .clr(reset));  // open: en
  Adder #(.width(32)) adder_1 (.a(32'h1), .b(PC_q), .out(adder_1_out));  // open: cin, cout
  // Probe on PC_q
  // Probe on PC_q
  Shifter #(.width(32)) shifter_1 (.in(PC_q), .\dist (5'b00010), .out(shifter_1_out));
  InstructionMemory_main main_1 (.data_out(main_1_data_out));  // open: address
  Adder #(.width(32)) adder_2 (.a(shifter_1_out), .b(32'h4), .out(adder_2_out));  // open: cin, cout
  // Probe on \type 
  // Probe on instructiondecoder_1_rd
  // Probe on f3
  // Probe on instructiondecoder_1_rs1
  // Probe on instructiondecoder_1_rs2
  // Probe on f7
  // Probe on opcode
  // Probe on I_Imm
  // Probe on S_Imm
  // Probe on B_Imm
  // Probe on U_Imm
  // Probe on J_Imm
  BitSelector #(.width(7)) bitselector_1 (.in(opcode), .out(bitselector_1_out), .sel(3'b101));
  Adder #(.width(32)) adder_3 (.a(shifter_1_out), .b(U_Imm), .out(adder_3_out));  // open: cin, cout
  InstructionDecoder instructiondecoder_1 (
    .rd(instructiondecoder_1_rd), .funct3(f3), .rs1(instructiondecoder_1_rs1),
    .rs2(instructiondecoder_1_rs2), .funct7(f7), .opcode(opcode), .\type (\type ), .IImm(I_Imm),
    .SImm(S_Imm), .BImm(B_Imm), .UImm(U_Imm), .JImm(J_Imm), .Instruction(main_1_data_out));
  Decoder #(.select(3)) decoder_1 (
    .out0(R), .out1(I), .out2(dWrites[0]), .out3(B), .out4(U), .out5(J), .sel(\type ));  // open: out6, out7, en
  Multiplexer #(.enable("false"), .width(32)) multiplexer_2 (
    .in0(adder_3_out), .in1(U_Imm), .out(multiplexer_2_out), .sel(bitselector_1_out));
  Multiplexer #(.enable("false"), .width(32)) multiplexer_3 (
    .in0(multiplexer_7_out), .in1(adder_2_out), .out(multiplexer_3_out), .sel(push));
  Multiplexer #(.enable("false"), .width(32)) multiplexer_4 (
    .in0(multiplexer_3_out), .in1(multiplexer_2_out), .out(multiplexer_4_out), .sel(U));
  // Probe on opcode
  Clock Clock (.out(clk));
  RegFile_main main_2 (
    .rs1(main_2_rs1), .rs2(main_2_rs2), .sel_rs1(instructiondecoder_1_rs1),
    .sel_rs2(instructiondecoder_1_rs2), .write(wRD), .rd(instructiondecoder_1_rd), .rst(reset),
    .data(multiplexer_4_out), .clk(clk));
  or or_1 (push, J, jalr);
  Comparator #(.width(7)) comparator_1 (.a(opcode), .b(7'b0000011), .eq(loadData));  // open: gt, lt
  Comparator #(.width(7)) comparator_2 (.a(opcode), .b(7'b1100111), .eq(jalr));  // open: gt, lt
  or or_2 (wRD, R, I, U, J);
  Multiplexer #(.enable("false"), .width(32)) multiplexer_5 (
    .in0(main_2_rs1), .in1(shifter_1_out), .out(multiplexer_5_out), .sel(usePC));
  or or_3 (usePC, B, U, J);
  // Probe on multiplexer_5_out
  // Probe on multiplexer_6_out
  Multiplexer #(.enable("false"), .select(3), .width(32)) multiplexer_6 (
    .in0(main_2_rs2), .in1(I_Imm), .in2(S_Imm), .in3(B_Imm), .in4(U_Imm), .in5(J_Imm),
    .out(multiplexer_6_out), .sel(\type ));  // open: in6, in7
  BranchCalc_main main_3 (.Take_branch(takeBranch), .rs1(main_2_rs1), .rs2(main_2_rs2), .f3(f3), .b_type(B));
  or or_4 (fADD, dWrites[0], B, J, loadData);
  ALU_main main_4 (
    .d(main_4_d), .s1(multiplexer_5_out), .s2(multiplexer_6_out), .funct7(f7), .AddOveride(fADD), .funct3(f3));
  or or_5 (ALUToPC, takeBranch, J, jalr);
  Shifter #(.shift("lr"), .width(32)) shifter_2 (.in(main_4_d), .\dist (5'b00010), .out(shifter_2_out));
  // Probe on main_4_d
  STypeSelector_main main_5 (.out_2(dWrites[4:1]));  // open: in_1
  // Probe on main_6_data_out
  DataMemory_main main_6 (
    .data_out(main_6_data_out), .address(main_4_d), .byte_writes(dWrites), .clk(clk), .data_in(main_2_rs2));
  LoadSelector_main main_7 (.out_3(main_7_out_3));  // open: in_1, in_2
  // Probe on main_7_out_3
  // Probe on multiplexer_7_out
  Multiplexer #(.enable("false"), .width(32)) multiplexer_7 (
    .in0(main_4_d), .in1(main_7_out_3), .out(multiplexer_7_out), .sel(loadData));

  // Other names for the same wires on the sheet: S = dWrites[0]; rst = reset

  // Notes on the sheet:
  //   Add 1 because IMem 
  //   is accessible only in 
  //   multiples of 4 bytes 
  //   (since all instructions 
  //   are 32bits exactly)
  //   Shift back to byte addressed
  //   R
  //   I
  //   S
  //   B
  //   U
  //   J
  //   R
  //   I
  //   S
  //   B
  //   U
  //   J
  //   R
  //   I
  //   S
  //   B
  //   U
  //   J
  //   Shift back to inst addressed
  //   (multiples of 4 bytes)
  //   R
  //   I
  //   S
  //   B
  //   U
  //   J
endmodule
