// Logisim project STypeSelector.circ as structural Verilog: 1 circuit, main circuit main
module main (
  input  [2:0] in_1,
  output [3:0] out_2
);

  wire [1:0] bitselector_1_out;

  // Probe on bitselector_1_out
  BitSelector #(.group(2), .width(3)) bitselector_1 (.in(in_1), .out(bitselector_1_out), .sel(1'b0));
  Multiplexer #(.enable("false"), .select(2), .width(4)) multiplexer_1 (
    .in0(4'b0001), .in1(4'b0011), .in2(4'b1111), .in3(4'b0000), .out(out_2), .sel(bitselector_1_out));
endmodule
